// Logisim project 7SegmentKhatera.circ as structural Verilog: 1 circuit, main circuit main
module main (
  input  C,
  input  B,
  input  A,
  input  D,
  input  CLK,
  output out_6,
  output out_7,
  output out_8,
  output out_9,
  output out_10,
  output out_11,
  output out_12,
  output MUX
);

  wire _1_out, _2_out, _3_out, _4_out, _5_out, _6_out, _7_out, _8_out, _9_out, _10_out, _12_out, _13_out,
       _14_out, _15_out, _16_out;
  wire [2:0] counter_1_q;

  and _1 (_1_out, B, ~D);  // AND_Gate
  and _2 (_2_out, A, C, ~D);  // AND_Gate
  and _3 (_3_out, ~A, ~B, ~C);  // AND_Gate
  and _4 (_4_out, ~B, ~C, D);  // AND_Gate
  and _5 (_5_out, ~A, ~B, ~D);  // AND_Gate
  and _6 (_6_out, A, ~B, ~C);  // AND_Gate
  and _7 (_7_out, A, B, ~D);  // AND_Gate
  and _8 (_8_out, B, ~C, ~D);  // AND_Gate
  and _9 (_9_out, ~B, ~D);  // AND_Gate
  and _10 (_10_out, B, C, ~D);  // AND_Gate
  // AND_Gate _11 has open pins: in0=A, in1=B, in2=D, out=open
  and _12 (_12_out, A, ~B, C, ~D);  // AND_Gate
  and _13 (_13_out, ~A, B, ~D);  // AND_Gate
  and _14 (_14_out, ~B, C, ~D);  // AND_Gate
  and _15 (_15_out, ~A, C, ~D);  // AND_Gate
  and _16 (_16_out, ~B, C, ~D);  // AND_Gate
  or or_1 (out_6, _1_out, _2_out, _3_out, _4_out);
  or or_2 (out_7, _3_out, _5_out, _6_out, _7_out, _8_out);
  or or_3 (out_8, _3_out, _9_out, _6_out, _10_out, _7_out);
  or or_4 (out_9, _3_out, _4_out, _13_out, _8_out, _12_out);
  or or_5 (out_10, _3_out, _13_out);
  or or_6 (out_11, _3_out, _4_out, _14_out, _15_out);
  or or_7 (out_12, _16_out, _4_out, _13_out, _8_out);
  Counter #(.width(3), .max('h6)) counter_1 (.Q(counter_1_q), .clk(CLK));  // open: load, D, count, carry, clr
  Multiplexer #(.select(3)) multiplexer_1 (
    .in0(out_6), .in1(out_7), .in2(out_8), .in3(out_9), .in4(out_10), .in5(out_11), .in6(out_12), .out(MUX),
    .sel(counter_1_q));  // open: in7, en
endmodule
