// Logisim project Ampel_nicht_ganz_so_gut.circ as structural Verilog: 1 circuit, main circuit main
module main (
  input  P
);

  wire _5_out, _6_out, _11_out, _41_out, _46_out, _47_out, _77_out, and_1_out, and_2_out, and_3_out,
       and_4_out, and_5_out, and_6_out, and_7_out, and_8_out, and_9_out, and_10_out, and_11_out, clock_1_out,
       counter_1_carry, idle_out, or_1_out, or_2_out, or_3_out, or_4_out, or_5_out, or_6_out, or_7_out,
       or_8_out, or_9_out, or_10_out, Z0_q, Z1_q, Z2_q;
  wire [7:0] counter_2_q;

  Clock clock_1 (.out(clock_1_out));
  Counter #(.width(9), .max('h1ff)) counter_1 (
    .count(P), .carry(counter_1_carry), .clk(clock_1_out));  // open: load, D, Q, clr
  Counter #(.max('h4d)) counter_2 (.Q(counter_2_q), .clk(counter_1_carry));  // open: load, D, count, carry, clr
  and _5 (_5_out, counter_2_q[0], ~counter_2_q[1], counter_2_q[2], ~counter_2_q[3], ~counter_2_q[4], ~counter_2_q[5], ~counter_2_q[6], ~counter_2_q[7]);  // AND_Gate
  and _6 (_6_out, ~counter_2_q[0], counter_2_q[1], counter_2_q[2], ~counter_2_q[3], ~counter_2_q[4], ~counter_2_q[5], ~counter_2_q[6], ~counter_2_q[7]);  // AND_Gate
  and _11 (_11_out, counter_2_q[0], counter_2_q[1], ~counter_2_q[2], counter_2_q[3], ~counter_2_q[4], ~counter_2_q[5], ~counter_2_q[6], ~counter_2_q[7]);  // AND_Gate
  and _41 (_41_out, counter_2_q[0], ~counter_2_q[1], ~counter_2_q[2], counter_2_q[3], ~counter_2_q[4], counter_2_q[5], ~counter_2_q[6], ~counter_2_q[7]);  // AND_Gate
  and _46 (_46_out, ~counter_2_q[0], counter_2_q[1], counter_2_q[2], counter_2_q[3], ~counter_2_q[4], counter_2_q[5], ~counter_2_q[6], ~counter_2_q[7]);  // AND_Gate
  and _47 (_47_out, counter_2_q[0], counter_2_q[1], counter_2_q[2], counter_2_q[3], ~counter_2_q[4], counter_2_q[5], ~counter_2_q[6], ~counter_2_q[7]);  // AND_Gate
  and _77 (_77_out, counter_2_q[0], ~counter_2_q[1], counter_2_q[2], counter_2_q[3], ~counter_2_q[4], ~counter_2_q[5], counter_2_q[6], ~counter_2_q[7]);  // AND_Gate
  and idle (idle_out, ~counter_2_q[0], ~counter_2_q[1], ~counter_2_q[2], ~counter_2_q[3], ~counter_2_q[4], ~counter_2_q[5], ~counter_2_q[6], ~counter_2_q[7]);  // AND_Gate
  or or_1 (or_1_out, and_2_out, _5_out);
  or or_2 (or_2_out, and_3_out, _6_out);
  or or_3 (or_3_out, and_5_out, _11_out);
  or or_4 (or_4_out, and_6_out, _41_out);
  or or_5 (or_5_out, and_8_out, _46_out);
  or or_6 (or_6_out, and_10_out, _47_out);
  and and_1 (and_1_out, Z2_q, Z0_q);
  or or_7 (or_7_out, and_11_out, _77_out);
  and and_2 (and_2_out, Z0_q, ~_6_out);  // AND_Gate
  and and_3 (and_3_out, Z1_q, ~_11_out);  // AND_Gate
  and and_4 (and_4_out, Z0_q, Z1_q);
  and and_5 (and_5_out, and_4_out, ~_41_out);  // AND_Gate
  and and_6 (and_6_out, Z2_q, ~_46_out);  // AND_Gate
  and and_7 (and_7_out, Z0_q, Z1_q);
  and and_8 (and_8_out, and_7_out, ~_47_out);  // AND_Gate
  and and_9 (and_9_out, Z2_q, Z0_q);
  and and_10 (and_10_out, and_9_out, ~_77_out);  // AND_Gate
  and and_11 (and_11_out, and_1_out, ~idle_out);  // AND_Gate
  or or_8 (or_8_out, or_1_out, or_2_out, or_4_out);
  or or_9 (or_9_out, or_6_out, or_5_out, or_2_out, or_4_out, or_7_out);
  or or_10 (or_10_out, or_3_out, or_4_out);
  D_Flip_Flop Z0 (.clk(clock_1_out), .D(or_9_out), .Q(Z0_q));  // open: Qn, preset, en, reset
  D_Flip_Flop Z1 (.clk(clock_1_out), .D(or_8_out), .Q(Z1_q));  // open: Qn, preset, en, reset
  D_Flip_Flop Z2 (.clk(clock_1_out), .D(or_10_out), .Q(Z2_q));  // open: Qn, preset, en, reset
endmodule
