// Logisim project Pulserzeuger.circ as structural Verilog: 1 circuit, main circuit main
module main (
  input  E,
  output out_2
);

  wire clock_1_out, d_ff_1_q;

  Clock clock_1 (.out(clock_1_out));
  D_Flip_Flop d_ff_1 (.clk(clock_1_out), .D(E), .Q(d_ff_1_q));  // open: Qn, preset, en, reset
  and and_1 (out_2, E, ~d_ff_1_q);  // AND_Gate

  // Notes on the sheet:
  //   Pulserzeuger
endmodule
