// Logisim project Doppelfunktionstaste.circ as structural Verilog: 1 circuit, main circuit main
module main (
  input  S,
  input  E,
  output Start,
  output Stop,
  output Reset
);

  wire and_1_out, and_2_out, and_3_out, and_4_out, and_5_out, and_6_out, and_7_out, and_8_out, and_9_out,
       and_10_out, and_11_out, and_12_out, and_13_out, and_14_out, and_15_out, and_16_out, and_17_out,
       clock_1_out, d_ff_1_q, d_ff_2_q, or_1_out, or_2_out, or_3_out, Z0_q, Z1_q;

  Clock clock_1 (.out(clock_1_out));
  D_Flip_Flop d_ff_1 (.clk(or_1_out), .D(S), .Q(d_ff_1_q));  // open: Qn, preset, en, reset
  D_Flip_Flop d_ff_2 (.clk(or_1_out), .D(E), .Q(d_ff_2_q));  // open: Qn, preset, en, reset
  buf or_1 (or_1_out, clock_1_out);  // OR_Gate
  and and_1 (and_1_out, ~d_ff_1_q, S);  // AND_Gate
  and and_2 (and_2_out, ~d_ff_2_q, E);  // AND_Gate
  and and_3 (and_3_out, Z0_q, ~and_2_out, ~and_1_out);  // AND_Gate
  and and_4 (and_4_out, and_1_out, ~and_2_out, ~Z0_q);  // AND_Gate
  and and_5 (and_5_out, and_1_out, Z0_q, Z1_q);
  and and_6 (and_6_out, and_2_out, Z0_q, ~Z1_q);  // AND_Gate
  and and_7 (and_7_out, ~and_1_out, ~and_2_out, Z1_q);  // AND_Gate
  and and_8 (and_8_out, ~and_1_out, Z1_q, ~Z0_q);  // AND_Gate
  and and_9 (and_9_out, and_1_out, and_2_out, Z1_q);
  and and_10 (and_10_out, and_1_out, ~and_2_out, Z0_q, ~Z1_q);  // AND_Gate
  and and_11 (and_11_out, ~and_1_out, and_2_out, Z0_q, ~Z1_q);  // AND_Gate
  or or_2 (or_2_out, and_7_out, and_8_out, and_9_out, and_10_out, and_11_out);
  or or_3 (or_3_out, and_3_out, and_4_out, and_5_out, and_6_out);
  D_Flip_Flop Z0 (.clk(or_1_out), .D(or_3_out), .Q(Z0_q));  // open: Qn, preset, en, reset
  D_Flip_Flop Z1 (.clk(or_1_out), .D(or_2_out), .Q(Z1_q));  // open: Qn, preset, en, reset
  and and_12 (and_12_out, and_1_out, ~and_2_out, ~Z0_q);  // AND_Gate
  and and_13 (and_13_out, and_1_out, ~and_2_out, Z1_q);  // AND_Gate
  and and_14 (and_14_out, ~and_1_out, and_2_out, Z0_q, ~Z1_q);  // AND_Gate
  and and_15 (and_15_out, and_1_out, ~and_2_out, Z0_q, ~Z1_q);  // AND_Gate
  and and_16 (and_16_out, ~and_1_out, and_2_out, Z0_q, Z1_q);  // AND_Gate
  and and_17 (and_17_out, and_1_out, ~and_2_out, Z0_q, Z1_q);  // AND_Gate
  or or_4 (Start, and_12_out, and_13_out);
  or or_5 (Stop, and_14_out, and_15_out);
  or or_6 (Reset, and_16_out, and_17_out);

  // Notes on the sheet:
  //   S
  //   Z1
  //   Z0
  //   E
  //   E
  //   S
  //   Z1
  //   Z0
  //   Z1
  //   E
  //   S
  //   Z0
endmodule
