// Logisim project Stoppuhr.circ as structural Verilog: 1 circuit, main circuit main
module main (
);

  wire and_1_out, clock_1_out, counter_2_carry, counter_3_carry, counter_4_carry, counter_5_carry,
       counter_7_carry, d_ff_1_q, d_ff_2_q, d_ff_3_q, d_ff_4_q, d_ff_5_q, d_ff_6_q, main_1_p4, main_1_p5,
       main_1_p6, not_1_out, or_1_out, START_out, STOPP_out;
  wire [1:0] counter_1_q;
  wire [3:0] counter_3_q, counter_4_q, counter_5_q, counter_6_q, multiplexer_1_out;
  wire [6:0] demultiplexer_1_out0, demultiplexer_1_out1, demultiplexer_1_out2, demultiplexer_1_out3,
       main_2_out_5;

  Clock clock_1 (.out(clock_1_out));
  Button START (.out(START_out));
  Button STOPP (.out(STOPP_out));
  Counter #(.width(2), .max('h3)) counter_1 (.Q(counter_1_q), .clk(clock_1_out));  // open: load, D, count, carry, clr
  _7_Segment_Display u_7_segment_display_1 (
    .g(demultiplexer_1_out3[6]), .f(demultiplexer_1_out3[5]), .a(demultiplexer_1_out3[0]),
    .b(demultiplexer_1_out3[1]), .e(demultiplexer_1_out3[4]), .d(demultiplexer_1_out3[3]),
    .c(demultiplexer_1_out3[2]));  // open: dp
  Multiplexer #(.select(2), .width(4)) multiplexer_1 (
    .in0(counter_3_q), .in1(counter_4_q), .in2(counter_5_q), .in3(counter_6_q), .out(multiplexer_1_out),
    .sel(counter_1_q));  // open: en
  // Doppelfunktionstaste_main main_1: pin names not known; wires that end beside it: START_out, STOPP_out, clock_1_out, main_1_p4, main_1_p5, main_1_p6
  _7_Segment_Display u_7_segment_display_2 (
    .g(demultiplexer_1_out2[6]), .f(demultiplexer_1_out2[5]), .a(demultiplexer_1_out2[0]),
    .b(demultiplexer_1_out2[1]), .e(demultiplexer_1_out2[4]), .d(demultiplexer_1_out2[3]),
    .c(demultiplexer_1_out2[2]));  // open: dp
  and and_1 (and_1_out, d_ff_1_q, ~main_1_p5);  // AND_Gate
  or or_1 (or_1_out, main_1_p4, and_1_out);
  _7_Segment_Display u_7_segment_display_3 (
    .g(demultiplexer_1_out1[6]), .f(demultiplexer_1_out1[5]), .a(demultiplexer_1_out1[0]),
    .b(demultiplexer_1_out1[1]), .e(demultiplexer_1_out1[4]), .d(demultiplexer_1_out1[3]),
    .c(demultiplexer_1_out1[2]));  // open: dp
  D_Flip_Flop d_ff_1 (.clk(clock_1_out), .D(or_1_out), .Q(d_ff_1_q));  // open: Qn, preset, en, reset
  Counter #(.width(3), .max('h3)) counter_2 (
    .count(d_ff_1_q), .carry(counter_2_carry), .clk(clock_1_out), .clr(main_1_p6));  // open: load, D, Q
  Counter #(.width(4), .max('h9)) counter_3 (
    .Q(counter_3_q), .carry(counter_3_carry), .clk(d_ff_2_q), .clr(main_1_p6));  // open: load, D, count
  Counter #(.width(4), .max('h9)) counter_4 (
    .Q(counter_4_q), .carry(counter_4_carry), .clk(d_ff_3_q), .clr(main_1_p6));  // open: load, D, count
  Counter #(.width(4), .max('h9)) counter_5 (
    .Q(counter_5_q), .carry(counter_5_carry), .clk(d_ff_4_q), .clr(main_1_p6));  // open: load, D, count
  Counter #(.width(4), .max('h9)) counter_6 (
    .Q(counter_6_q), .clk(d_ff_5_q), .clr(main_1_p6));  // open: load, D, count, carry
  _7Segment_main main_2 (
    .D(multiplexer_1_out[3]), .C(multiplexer_1_out[2]), .B(multiplexer_1_out[1]), .A(multiplexer_1_out[0]),
    .out_5(main_2_out_5[0]), .out_6(main_2_out_5[1]), .out_7(main_2_out_5[2]), .out_8(main_2_out_5[3]),
    .out_9(main_2_out_5[4]), .out_10(main_2_out_5[5]), .out_11(main_2_out_5[6]));
  _7_Segment_Display u_7_segment_display_4 (
    .g(demultiplexer_1_out0[6]), .f(demultiplexer_1_out0[5]), .a(demultiplexer_1_out0[0]),
    .b(demultiplexer_1_out0[1]), .e(demultiplexer_1_out0[4]), .d(demultiplexer_1_out0[3]),
    .c(demultiplexer_1_out0[2]), .dp(d_ff_6_q));
  D_Flip_Flop d_ff_2 (.clk(clock_1_out), .D(counter_2_carry), .Q(d_ff_2_q));  // open: Qn, preset, en, reset
  D_Flip_Flop d_ff_3 (.clk(clock_1_out), .D(counter_3_carry), .Q(d_ff_3_q));  // open: Qn, preset, en, reset
  D_Flip_Flop d_ff_4 (.clk(clock_1_out), .D(counter_4_carry), .Q(d_ff_4_q));  // open: Qn, preset, en, reset
  D_Flip_Flop d_ff_5 (.clk(clock_1_out), .D(counter_5_carry), .Q(d_ff_5_q));  // open: Qn, preset, en, reset
  Demultiplexer #(.select(2), .width(7)) demultiplexer_1 (
    .out0(demultiplexer_1_out0), .out1(demultiplexer_1_out1), .out2(demultiplexer_1_out2),
    .out3(demultiplexer_1_out3), .in(main_2_out_5), .sel(counter_1_q));  // open: en
  D_Flip_Flop d_ff_6 (.clk(clock_1_out), .D(counter_7_carry), .Q(d_ff_6_q));  // open: Qn, preset, en, reset
  not not_1 (not_1_out, d_ff_1_q);
  Counter #(.max('h80)) counter_7 (
    .count(not_1_out), .carry(counter_7_carry), .clk(clock_1_out));  // open: load, D, Q, clr
endmodule
