// Logisim project stoppuhrKhatera.circ as structural Verilog: 1 circuit, main circuit main
module main (
  input  Start,
  input  Stopp
);

  wire and_1_out, clock_1_out, counter_1_carry, counter_2_carry, counter_3_carry, counter_4_carry,
       counter_6_carry, d_ff_1_q, d_ff_2_q, d_ff_3_q, d_ff_4_q, d_ff_5_q, d_ff_6_q, main_1_out_6,
       main_1_out_7, main_1_out_8, main_1_out_9, main_1_out_10, main_1_out_11, main_1_out_12, main_2_reset,
       main_2_start, main_2_stop, main_3_out_6, main_3_out_7, main_3_out_8, main_3_out_9, main_3_out_10,
       main_3_out_11, main_3_out_12, main_4_out_6, main_4_out_7, main_4_out_8, main_4_out_9, main_4_out_10,
       main_4_out_11, main_4_out_12, main_5_out_6, main_5_out_7, main_5_out_8, main_5_out_9, main_5_out_10,
       main_5_out_11, main_5_out_12, not_1_out, or_1_out;
  wire [3:0] counter_2_q, counter_3_q, counter_4_q, counter_5_q;

  Clock clock_1 (.out(clock_1_out));
  _7SegmentKhatera_main main_1 (
    .D(counter_5_q[3]), .C(counter_5_q[2]), .B(counter_5_q[1]), .A(counter_5_q[0]), .out_6(main_1_out_6),
    .out_7(main_1_out_7), .out_8(main_1_out_8), .out_9(main_1_out_9), .out_10(main_1_out_10),
    .out_11(main_1_out_11), .out_12(main_1_out_12));  // open: CLK, MUX
  _7_Segment_Display u_7_segment_display_1 (
    .g(main_1_out_12), .f(main_1_out_11), .a(main_1_out_6), .b(main_1_out_7), .e(main_1_out_10),
    .d(main_1_out_9), .c(main_1_out_8));  // open: dp
  stoppuhr_neuuuuu_main main_2 (
    .S(Start), .E(Stopp), .a(clock_1_out), .Start(main_2_start), .Stop(main_2_stop), .Reset(main_2_reset));
  _7_Segment_Display u_7_segment_display_2 (
    .g(main_3_out_12), .f(main_3_out_11), .a(main_3_out_6), .b(main_3_out_7), .e(main_3_out_10),
    .d(main_3_out_9), .c(main_3_out_8));  // open: dp
  _7SegmentKhatera_main main_3 (
    .D(counter_4_q[3]), .C(counter_4_q[2]), .B(counter_4_q[1]), .A(counter_4_q[0]), .out_6(main_3_out_6),
    .out_7(main_3_out_7), .out_8(main_3_out_8), .out_9(main_3_out_9), .out_10(main_3_out_10),
    .out_11(main_3_out_11), .out_12(main_3_out_12));  // open: CLK, MUX
  and and_1 (and_1_out, d_ff_1_q, ~main_2_stop);  // AND_Gate
  or or_1 (or_1_out, main_2_start, and_1_out);
  _7SegmentKhatera_main main_4 (
    .D(counter_3_q[3]), .C(counter_3_q[2]), .B(counter_3_q[1]), .A(counter_3_q[0]), .out_6(main_4_out_6),
    .out_7(main_4_out_7), .out_8(main_4_out_8), .out_9(main_4_out_9), .out_10(main_4_out_10),
    .out_11(main_4_out_11), .out_12(main_4_out_12));  // open: CLK, MUX
  _7_Segment_Display u_7_segment_display_3 (
    .g(main_4_out_12), .f(main_4_out_11), .a(main_4_out_6), .b(main_4_out_7), .e(main_4_out_10),
    .d(main_4_out_9), .c(main_4_out_8));  // open: dp
  D_Flip_Flop d_ff_1 (.clk(clock_1_out), .D(or_1_out), .Q(d_ff_1_q));  // open: Qn, preset, en, reset
  Counter #(.width(3), .max('h3)) counter_1 (
    .count(d_ff_1_q), .carry(counter_1_carry), .clk(clock_1_out), .clr(main_2_reset));  // open: load, D, Q
  Counter #(.width(4), .max('h9)) counter_2 (
    .Q(counter_2_q), .carry(counter_2_carry), .clk(d_ff_2_q), .clr(main_2_reset));  // open: load, D, count
  Counter #(.width(4), .max('h9)) counter_3 (
    .Q(counter_3_q), .carry(counter_3_carry), .clk(d_ff_3_q), .clr(main_2_reset));  // open: load, D, count
  Counter #(.width(4), .max('h9)) counter_4 (
    .Q(counter_4_q), .carry(counter_4_carry), .clk(d_ff_4_q), .clr(main_2_reset));  // open: load, D, count
  Counter #(.width(4), .max('h9)) counter_5 (
    .Q(counter_5_q), .clk(d_ff_5_q), .clr(main_2_reset));  // open: load, D, count, carry
  _7SegmentKhatera_main main_5 (
    .D(counter_2_q[3]), .C(counter_2_q[2]), .B(counter_2_q[1]), .A(counter_2_q[0]), .out_6(main_5_out_6),
    .out_7(main_5_out_7), .out_8(main_5_out_8), .out_9(main_5_out_9), .out_10(main_5_out_10),
    .out_11(main_5_out_11), .out_12(main_5_out_12));  // open: CLK, MUX
  _7_Segment_Display u_7_segment_display_4 (
    .g(main_5_out_12), .f(main_5_out_11), .a(main_5_out_6), .b(main_5_out_7), .e(main_5_out_10),
    .d(main_5_out_9), .c(main_5_out_8), .dp(d_ff_6_q));
  D_Flip_Flop d_ff_2 (.clk(clock_1_out), .D(counter_1_carry), .Q(d_ff_2_q));  // open: Qn, preset, en, reset
  D_Flip_Flop d_ff_3 (.clk(clock_1_out), .D(counter_2_carry), .Q(d_ff_3_q));  // open: Qn, preset, en, reset
  D_Flip_Flop d_ff_4 (.clk(clock_1_out), .D(counter_3_carry), .Q(d_ff_4_q));  // open: Qn, preset, en, reset
  D_Flip_Flop d_ff_5 (.clk(clock_1_out), .D(counter_4_carry), .Q(d_ff_5_q));  // open: Qn, preset, en, reset
  D_Flip_Flop d_ff_6 (.clk(clock_1_out), .D(counter_6_carry), .Q(d_ff_6_q));  // open: Qn, preset, en, reset
  not not_1 (not_1_out, d_ff_1_q);
  Counter #(.max('h80)) counter_6 (
    .count(not_1_out), .carry(counter_6_carry), .clk(clock_1_out));  // open: load, D, Q, clr
endmodule
